# Fritzing sketch simon_diagram (saved by Fritzing 0.9.4)
breadboards: 1

parts:
  Adafruit_HUZZAH_ESP8266_Breakout1 = Adafruit HUZZAH ESP8266 Breakout [part_number=2471]
  S5 = Momentary Switch [package=ksa_sealed_tac_switch]
  S6 = Momentary Switch [package=ksa_sealed_tac_switch]
  S7 = Momentary Switch [package=ksa_sealed_tac_switch]
  S8 = Momentary Switch [package=ksa_sealed_tac_switch]
  R1 = Resistor [tolerance=±5% resistance=10k package="0603 [SMD]"]
  R2 = Resistor [tolerance=±5% resistance=10k package="0603 [SMD]"]
  R3 = Resistor [tolerance=±5% resistance=10k package="0603 [SMD]"]
  R4 = Resistor [tolerance=±5% resistance=10k package="0603 [SMD]"]
  LED1 = LED - 5mm [color="Green (560nm)" package="5 mm [THT]"]
  LED2 = LED - 5mm [color="Red (633nm)" package="5 mm [THT]"]
  LED3 = LED - 5mm [color="Blue (470nm)" package="5 mm [THT]"]
  LED4 = LED - 5mm [color="Yellow (585nm)" package="5 mm [THT]"]
  R5 = Resistor [tolerance=±5% resistance=10k package="0603 [SMD]"]
  R6 = Resistor [tolerance=±5% resistance=10k package="0603 [SMD]"]
  R7 = Resistor [tolerance=±5% resistance=10k package="0603 [SMD]"]
  R8 = Resistor [tolerance=±5% resistance=10k package="0603 [SMD]"]
  J1 = Piezo Speaker

nets:
  N1: Adafruit_HUZZAH_ESP8266_Breakout1.GND, S6.3, S7.3, S8.3, LED2.cathode, LED3.cathode, LED4.cathode, J1.pin1
  N2: Adafruit_HUZZAH_ESP8266_Breakout1.#13, R5.Pin_1
  N3: Adafruit_HUZZAH_ESP8266_Breakout1.#12, R6.Pin_1
  N4: Adafruit_HUZZAH_ESP8266_Breakout1.#14, R8.Pin_1
  N5: Adafruit_HUZZAH_ESP8266_Breakout1.#16, S6.2, R2.Pin_0
  N6: Adafruit_HUZZAH_ESP8266_Breakout1.#5, S8.2, R4.Pin_0
  N7: Adafruit_HUZZAH_ESP8266_Breakout1.#4, S7.2, R3.Pin_0
  N8: Adafruit_HUZZAH_ESP8266_Breakout1.#0, J1.pin2
  N9: Adafruit_HUZZAH_ESP8266_Breakout1.#2, S5.2, R1.Pin_0
  N10: Adafruit_HUZZAH_ESP8266_Breakout1.#15, R7.Pin_1
  N11: Adafruit_HUZZAH_ESP8266_Breakout1.3V, R1.Pin_1, R2.Pin_1, R3.Pin_1, R4.Pin_1
  N12: S5.3, LED1.cathode
  N13: LED1.anode, R5.Pin_0
  N14: LED2.anode, R6.Pin_0
  N15: LED3.anode, R7.Pin_0
  N16: LED4.anode, R8.Pin_0
